# Fritzing sketch Montagem_RTC (saved by Fritzing 0.9.3b)
breadboards: 1

parts:
  Componente1 = Arduino Nano (Rev3.0)
  S1 = Pushbutton [package="[SMD]"]
  S2 = Pushbutton [package="[SMD]"]
  R1 = Resistor [tolerance=±5% resistance=101 package="0603 [SMD]"]
  R2 = Resistor [tolerance=±5% resistance=510 package="0603 [SMD]"]
  LCD1 = LCD screen
  J1 = Piezo Speaker
  ZS-042_RTC1 = ZS-042 RTC Module  # not connected
  LCM1602_IIC1 = LCM1602 IIC [part_number="LCM1602 IIC" chip_label="LCM1602 IIC" package="DIP (Dual Inline) [THT]"]

nets:
  GND: Componente1.GND, R1.Pin_0, J1.pin1, LCM1602_IIC1.GND
  N1: Componente1.D3, J1.pin2
  5V: Componente1.5V, S1.Pin_1, S1.Pin_2, LCM1602_IIC1.VCC
  N2: Componente1.A5, LCM1602_IIC1.SCL
  N3: Componente1.A4, LCM1602_IIC1.SDA
  N4: Componente1.A0, S2.Pin_3, S2.Pin_4, R1.Pin_1, R2.Pin_0
  N5: S1.Pin_3, S1.Pin_4, R2.Pin_1
  N6: S2.Pin_1, S2.Pin_2
  VSS: LCD1.VSS, LCM1602_IIC1.VSS
  VDD: LCD1.VDD, LCM1602_IIC1.VDD
  N7: LCD1.V0, LCM1602_IIC1.V0
  N8: LCD1.RS, LCM1602_IIC1.RS
  N9: LCD1.R/W, LCM1602_IIC1.RW
  N10: LCD1.E, LCM1602_IIC1.E
  N11: LCD1.DB0, LCM1602_IIC1.D0
  N12: LCD1.DB1, LCM1602_IIC1.D1
  N13: LCD1.DB2, LCM1602_IIC1.D2
  N14: LCD1.DB3, LCM1602_IIC1.D3
  N15: LCD1.DB4, LCM1602_IIC1.D4
  N16: LCD1.DB5, LCM1602_IIC1.D5
  N17: LCD1.DB6, LCM1602_IIC1.D6
  N18: LCD1.DB7, LCM1602_IIC1.D7
  N19: LCD1.LED+, LCM1602_IIC1.A
  N20: LCD1.LED-, LCM1602_IIC1.K

custom parts:
  LCM1602 IIC: I2C-Module to use a 1602 or 2004 LCD on with the wire.h libory Serial LCD Modul
